// Logisim project Prac4APart1-MHTRON001.circ as structural Verilog: 1 circuit, main circuit main
module main (
  input  I,
  input  in_2,
  output O3,
  output O2,
  output O1,
  output O0
);

  wire and_1_out, and_2_out, and_3_out, and_4_out, and_5_out, and_6_out, clock_1_out, d_ff_1_q, d_ff_2_q,
       d_ff_2_qn, not_1_out, not_2_out, or_1_out, or_2_out;

  Clock clock_1 (.out(clock_1_out));
  not not_1 (not_1_out, I);
  and and_1 (and_1_out, d_ff_1_q, d_ff_2_q, I);
  and and_2 (and_2_out, not_1_out, O1, O1);
  and and_3 (and_3_out, O1, d_ff_2_qn);
  or or_1 (or_1_out, and_1_out, and_2_out, and_3_out);
  D_Flip_Flop d_ff_1 (.clk(clock_1_out), .D(or_1_out), .Q(d_ff_1_q), .Qn(O1));  // open: preset, en, reset
  not not_2 (not_2_out, I);
  and and_4 (and_4_out, d_ff_2_q, not_2_out, O1);
  and and_5 (and_5_out, d_ff_1_q, d_ff_2_qn);
  and and_6 (and_6_out, I, d_ff_2_qn);
  or or_2 (or_2_out, and_4_out, and_5_out, and_6_out);
  D_Flip_Flop d_ff_2 (.clk(clock_1_out), .D(or_2_out), .Q(d_ff_2_q), .Qn(d_ff_2_qn));  // open: preset, en, reset
  and and_7 (O3, d_ff_2_q, d_ff_1_q);
  xor xor_1 (O2, d_ff_1_q, d_ff_2_q);

  assign O0 = in_2;

  // Notes on the sheet:
  //   CLK
  //   Q0
  //   Q1
endmodule
