// Logisim project Prac4APart2-MHTRON001.circ as structural Verilog: 1 circuit, main circuit main
module main (
  input  I1,
  input  I2,
  output out_3,
  output out_4,
  output out_5,
  output out_6
);

  wire and_1_out, and_3_out, and_4_out, clock_1_out, not_1_out, not_2_out, not_3_out;

  Clock clock_1 (.out(clock_1_out));
  D_Flip_Flop d_ff_1 (.clk(clock_1_out), .D(out_4), .Q(out_6));  // open: Qn, preset, en, reset
  not not_1 (not_1_out, I1);
  and and_1 (and_1_out, I1, out_6);
  and and_2 (out_4, out_6, not_1_out);
  D_Flip_Flop d_ff_2 (.clk(clock_1_out), .D(and_1_out), .Q(out_5));  // open: Qn, preset, en, reset
  not not_2 (not_2_out, I1);
  and and_3 (and_3_out, I1, out_5);
  and and_4 (and_4_out, out_5, not_2_out);
  D_Flip_Flop d_ff_3 (.clk(clock_1_out), .D(and_4_out), .Q(out_4));  // open: Qn, preset, en, reset
  D_Flip_Flop d_ff_4 (.clk(clock_1_out), .D(and_3_out), .Q(out_3));  // open: Qn, preset, en, reset
  not not_3 (not_3_out, I2);
  and and_5 (out_4, I2, out_3);
  and and_6 (and_3_out, out_3, not_3_out);

  // Notes on the sheet:
  //   CLK
endmodule
