// Logisim project Prac5_MHTRON001_NDXVIK005.circ as structural Verilog: 7 circuits, main circuit main
module main (
  input  A0,
  input  A1,
  input  B0,
  input  B1,
  input  F0,
  input  F1,
  input  F2
);

  wire alu_1_y0, alu_1_y1;

  ALU alu_1 (.A0(A0), .A1(A1), .B0(B0), .B1(B1), .F0(F0), .F1(F1), .F2(F2), .Y0(alu_1_y0), .Y1(alu_1_y1));
  LED Y0 (.in(alu_1_y0));
  LED Y1 (.in(alu_1_y1));
endmodule

module ALU (
  input  A0,
  input  A1,
  input  B0,
  input  B1,
  input  F0,
  input  F1,
  input  F2,
  output Y0,
  output Y1
);

  wire Adder_Subtractor_cout, Adder_Subtractor_s0, Adder_Subtractor_s1, bitAND_y0, bitAND_y1, bitor_1_y0,
       bitor_1_y1, divide_2_1_y0, divide_2_1_y1, multiplexer_1_out, multiplexer_2_out, multiplexer_3_out,
       multiplexer_4_out, multiplexer_5_out, multiplexer_6_out, multiplexer_7_out, multiplexer_8_out,
       multiplyx2_1_y0, multiplyx2_1_y1;

  Multiplexer #(.enable("false")) multiplexer_1 (.in0(B1), .in1(1'b0), .out(multiplexer_1_out), .sel(F1));
  Multiplyx2 multiplyx2_1 (.Y1(multiplyx2_1_y1), .Y0(multiplyx2_1_y0), .A1(A1), .A0(A0));
  Multiplexer #(.enable("false")) multiplexer_2 (.in0(B0), .in1(1'b1), .out(multiplexer_2_out), .sel(F1));
  BitAND bitAND (.A0(A0), .B0(B0), .A1(A1), .B1(B1), .Y0(bitAND_y0), .Y1(bitAND_y1));
  bitOR bitor_1 (.A0(A0), .B0(B0), .A1(A1), .B1(B1), .Y0(bitor_1_y0), .Y1(bitor_1_y1));
  Divide_2 divide_2_1 (.Y0(divide_2_1_y0), .Y1(divide_2_1_y1), .A1(A1), .A0(A0));
  Adder_Subtractor Adder_Subtractor (
    .B0(multiplexer_2_out), .Sel(F0), .A1(A1), .B1(multiplexer_1_out), .S0(Adder_Subtractor_s0),
    .S1(Adder_Subtractor_s1), .Cout(Adder_Subtractor_cout), .A0(A0));
  Multiplexer #(.enable("false")) multiplexer_3 (.in0(bitAND_y0), .in1(bitor_1_y0), .out(multiplexer_3_out), .sel(F0));
  Multiplexer #(.enable("false")) multiplexer_4 (.in0(bitAND_y1), .in1(bitor_1_y1), .out(multiplexer_4_out), .sel(F0));
  Multiplexer #(.enable("false")) multiplexer_5 (
    .in0(multiplyx2_1_y0), .in1(divide_2_1_y0), .out(multiplexer_5_out), .sel(F0));
  Multiplexer #(.enable("false")) multiplexer_6 (
    .in0(multiplyx2_1_y1), .in1(divide_2_1_y1), .out(multiplexer_6_out), .sel(F0));
  LED led_1 (.in(Adder_Subtractor_cout));
  Multiplexer #(.enable("false")) multiplexer_7 (
    .in0(multiplexer_5_out), .in1(multiplexer_3_out), .out(multiplexer_7_out), .sel(F1));
  Multiplexer #(.enable("false")) multiplexer_8 (
    .in0(multiplexer_6_out), .in1(multiplexer_4_out), .out(multiplexer_8_out), .sel(F1));
  Multiplexer #(.enable("false")) multiplexer_9 (
    .in0(Adder_Subtractor_s0), .in1(multiplexer_7_out), .out(Y0), .sel(F2));
  Multiplexer #(.enable("false")) multiplexer_10 (
    .in0(Adder_Subtractor_s1), .in1(multiplexer_8_out), .out(Y1), .sel(F2));
endmodule

module Adder_Subtractor (
  input  A0,
  input  B0,
  input  Sel,
  input  A1,
  input  B1,
  output S0,
  output S1,
  output Cout
);

  wire adder_1_cout, xor_1_out, xor_2_out;

  xor xor_1 (xor_1_out, B0, Sel);
  xor xor_2 (xor_2_out, B1, Sel);
  Adder #(.width(1)) adder_1 (.a(A0), .b(xor_1_out), .out(S0), .cin(Sel), .cout(adder_1_cout));
  Adder #(.width(1)) adder_2 (.a(A1), .b(xor_2_out), .out(S1), .cin(adder_1_cout), .cout(Cout));

  // Notes on the sheet:
  //   Sel=0:adder
  //   Sel=1:subtractor
  //   for INCREMENT / DECREMENT set (B1and B0) to (1)
  //   and choose select line for + (increment) or - (decrement)
endmodule

module BitAND (
  input  A0,
  input  B0,
  input  A1,
  input  B1,
  output Y0,
  output Y1
);

  and and_1 (Y0, A0, B0);
  and and_2 (Y1, A1, B1);
endmodule

module bitOR (
  input  A0,
  input  B0,
  input  A1,
  input  B1,
  output Y0,
  output Y1
);

  or or_1 (Y0, A0, B0);
  or or_2 (Y1, A1, B1);
endmodule

// X2
module Multiplyx2 (
  input  A1,
  input  A0,
  output Y1,
  output Y0
);

  Multiplexer #(.enable("false")) multiplexer_1 (.in0(A1), .in1(A0), .out(Y1), .sel(1'b1));
  Multiplexer #(.enable("false")) multiplexer_2 (.in0(A0), .in1(1'b0), .out(Y0), .sel(1'b1));
endmodule

// /2
module Divide_2 (
  input  A1,
  input  A0,
  output Y0,
  output Y1
);

  Multiplexer #(.enable("false")) multiplexer_1 (.in0(A0), .in1(A1), .out(Y0), .sel(1'b1));
  Multiplexer #(.enable("false")) multiplexer_2 (.in0(A1), .in1(1'b0), .out(Y1), .sel(1'b1));
endmodule
